// Logisim project assignment1.circ as structural Verilog: 1 circuit, main circuit main
module main (
  input  in_1,
  input  in_2,
  input  in_3,
  input  [3:0] Selection_bit,
  output I,
  output Z,
  output S
);

  wire and_2_out, and_3_out, and_4_out, and_5_out, and_6_out, and_7_out, clock_1_out, clock_2_out,
       decoder_1_out1, decoder_1_out3, decoder_1_out4, decoder_1_out5, decoder_1_out6, decoder_1_out7,
       decoder_2_out1, decoder_2_out2, decoder_2_out3, decoder_2_out4, decoder_2_out6, decoder_3_out1,
       decoder_3_out2, decoder_3_out3, decoder_3_out4, decoder_3_out6, not_2_out, not_4_out, not_5_out,
       not_6_out, or_2_out, or_3_out, or_4_out, or_6_out;
  wire [1:0] decoder_2_out7, not_3_out;
  wire [2:0] CDR_q_3, CDR_q_4, CDR_q_5;
  wire [5:2] register_3_q_2;
  wire [6:0] adder_6_out, CAR_q, CDR_q, multiplexer_8_out, SBR_q;
  wire [10:0] adder_1_out, adder_2_out, multiplexer_1_out, multiplexer_2_out, multiplexer_3_out,
       register_1_q, register_2_q, register_3_q;
  wire [10:7] CDR_q_2;
  wire [14:0] register_4_q;
  wire [15:0] adder_3_out, adder_4_out, adder_5_out, and_1_out, multiplexer_4_out, multiplexer_5_out,
       multiplexer_6_out, multiplexer_7_out, not_1_out, or_1_out, ram_1_data, shifter_1_out, shifter_2_out,
       subtractor_1_out, xor_1_out;
  wire [19:0] rom_1_data;

  Clock clock_1 (.out(clock_1_out));
  Adder #(.width(11)) adder_1 (.a(register_1_q), .b(11'h1), .out(adder_1_out));  // open: cin, cout
  Multiplexer #(.width(11)) multiplexer_1 (
    .in0(multiplexer_2_out), .in1(adder_1_out), .out(multiplexer_1_out));  // open: sel, en
  Multiplexer #(.width(11)) multiplexer_2 (
    .in0(register_2_q), .in1(register_3_q), .out(multiplexer_2_out), .sel(decoder_1_out4));  // open: en
  Register #(.width(11)) register_1 (
    .D(multiplexer_1_out), .en(or_4_out), .Q(register_1_q), .clk(clock_1_out));  // open: clr
  Adder #(.width(11)) adder_2 (.a(register_2_q), .b(11'h1), .out(adder_2_out));  // open: cin, cout
  Adder #(.width(16)) adder_3 (
    .a({I, register_3_q_2, register_3_q}), .b({S, register_4_q}), .out(adder_3_out), .cin(in_3));  // open: cout
  Subtractor #(.width(16)) subtractor_1 (
    .a({I, register_3_q_2, register_3_q}), .b({S, register_4_q}), .out(subtractor_1_out), .bin(in_3));  // open: bout
  assign and_1_out = {I, register_3_q_2, register_3_q} & {S, register_4_q};  // AND_Gate and_1, 16 bits wide
  assign or_1_out = {I, register_3_q_2, register_3_q} | {S, register_4_q};  // OR_Gate or_1, 16 bits wide
  assign xor_1_out = {I, register_3_q_2, register_3_q} ^ {S, register_4_q};  // XOR_Gate xor_1, 16 bits wide
  assign not_1_out = ~{I, register_3_q_2, register_3_q};  // NOT_Gate not_1, 16 bits wide
  Shifter #(.width(16), .shift("lr")) shifter_1 (
    .in({I, register_3_q_2, register_3_q}), .\dist (4'b0001), .out(shifter_1_out));
  Shifter #(.width(16)) shifter_2 (.in({I, register_3_q_2, register_3_q}), .\dist (4'b0001), .out(shifter_2_out));
  Multiplexer #(.width(11)) multiplexer_3 (
    .in0(register_1_q), .in1(adder_2_out), .out(multiplexer_3_out), .sel(decoder_1_out5));  // open: en
  Register #(.width(11)) register_2 (.D(multiplexer_3_out), .en(decoder_3_out6), .Q(register_2_q));  // open: clk, clr
  Multiplexer #(.width(16)) multiplexer_4 (
    .in0(multiplexer_5_out), .in1(adder_4_out), .out(multiplexer_4_out), .sel(decoder_2_out6));  // open: en
  Adder #(.width(16)) adder_4 (.a({I, register_3_q_2, register_3_q}), .b(16'h1), .out(adder_4_out));  // open: cin, cout
  RAM #(.addrWidth(11), .dataWidth(16), .bus("separate")) ram_1 (
    .addr(register_1_q), .din({I, register_3_q_2, register_3_q}), .data(ram_1_data), .str(decoder_1_out7),
    .clk(clock_1_out), .ld(decoder_2_out4));  // open: sel, clr
  Register #(.width(16)) register_3 (
    .D(multiplexer_4_out), .en(or_3_out), .Q({I, register_3_q_2, register_3_q}));  // open: clk, clr
  Multiplexer #(.select(2), .width(16)) multiplexer_5 (
    .in0(ram_1_data), .in1({S, register_4_q}), .in2({{5{1'b0}}, register_2_q}), .out(multiplexer_5_out),
    .sel(decoder_2_out7));  // open: in3, en
  Multiplexer #(.select(4), .width(16)) multiplexer_6 (
    .in0(adder_3_out), .in1(subtractor_1_out), .in2(and_1_out), .in3(or_1_out), .in4(xor_1_out),
    .in5(not_1_out), .in6(shifter_1_out), .in7(shifter_2_out), .in8({I, register_3_q_2, register_3_q}),
    .out(multiplexer_6_out), .sel(Selection_bit));  // open: in9, in10, in11, in12, in13, in14, in15, en
  Adder #(.width(16)) adder_5 (.a({S, register_4_q}), .b(16'h1), .out(adder_5_out));  // open: cin, cout
  Multiplexer #(.width(16)) multiplexer_7 (
    .in0(multiplexer_6_out), .in1(adder_5_out), .out(multiplexer_7_out), .sel(decoder_1_out3));  // open: en
  Register #(.width(16)) register_4 (.D(multiplexer_7_out), .en(or_2_out), .Q({S, register_4_q}));  // open: clk, clr
  nor nor_1 (Z, register_4_q[0], register_4_q[1], register_4_q[2], register_4_q[3], register_4_q[4], register_4_q[5], register_4_q[6], register_4_q[7], register_4_q[9], register_4_q[10], register_4_q[11], register_4_q[12], register_4_q[13], register_4_q[14], S, register_4_q[8]);
  Register #(.width(7)) SBR (.Q(SBR_q));  // open: D, en, clk, clr
  not not_2 (not_2_out, CDR_q_2[8]);
  not not_3 (not_3_out[0], CDR_q_2[7]);
  not not_4 (not_4_out, CDR_q_2[10]);
  not not_5 (not_5_out, CDR_q_2[9]);
  or or_2 (or_2_out, decoder_1_out1, decoder_1_out3, decoder_1_out4, decoder_2_out1, decoder_2_out2, decoder_2_out3, decoder_3_out1, decoder_3_out2, decoder_3_out3, decoder_3_out4);
  or or_3 (or_3_out, decoder_2_out4, decoder_2_out7[1], decoder_2_out7[0]);
  or or_4 (or_4_out, decoder_1_out5, decoder_1_out6);
  and and_2 (and_2_out, I, not_4_out, not_5_out);
  and and_3 (and_3_out, S, not_5_out, CDR_q_2[10]);
  and and_4 (and_4_out, CDR_q_2[9], CDR_q_2[10]);
  and and_5 (and_5_out, not_4_out, CDR_q_2[9], Z);
  Adder #(.width(7)) adder_6 (.a(7'b0000001), .b(CAR_q), .out(adder_6_out));  // open: cin, cout
  or or_5 (not_3_out[1], and_6_out, and_7_out);
  or or_6 (or_6_out, and_2_out, and_3_out, and_4_out, and_5_out);
  // Probe on multiplexer_8_out
  Multiplexer #(.select(2), .width(7)) multiplexer_8 (
    .in0({in_2, register_3_q_2, {2{in_2}}}), .in1(adder_6_out), .in2(SBR_q), .in3(CDR_q),
    .out(multiplexer_8_out), .sel(not_3_out), .en(in_1));
  Clock clock_2 (.out(clock_2_out));
  and and_6 (and_6_out, not_2_out, CDR_q_2[7]);
  and and_7 (and_7_out, not_3_out[0], or_6_out);
  Register #(.width(7)) CAR (.D(multiplexer_8_out), .en(in_1), .Q(CAR_q), .clk(clock_2_out));  // open: clr
  not not_6 (not_6_out, clock_2_out);
  Decoder #(.select(3)) decoder_1 (
    .out1(decoder_1_out1), .out3(decoder_1_out3), .out4(decoder_1_out4), .out5(decoder_1_out5),
    .out6(decoder_1_out6), .out7(decoder_1_out7), .sel(CDR_q_5));  // open: out0, out2, en
  Decoder #(.select(3)) decoder_2 (
    .out1(decoder_2_out1), .out2(decoder_2_out2), .out3(decoder_2_out3), .out4(decoder_2_out4),
    .out5(decoder_2_out7[1]), .out6(decoder_2_out6), .out7(decoder_2_out7[0]), .sel(CDR_q_4));  // open: out0, en
  Decoder #(.select(3)) decoder_3 (
    .out1(decoder_3_out1), .out2(decoder_3_out2), .out3(decoder_3_out3), .out4(decoder_3_out4),
    .out6(decoder_3_out6), .sel(CDR_q_3));  // open: out0, out5, out7, en
  ROM #(.addrWidth(7), .dataWidth(20)) rom_1 (.addr(CAR_q), .data(rom_1_data));  // open: sel
  Register #(.width(20)) CDR (
    .D(rom_1_data), .en(in_1),
    .Q({CDR_q_5[0], CDR_q_5[1], CDR_q_5[2], CDR_q_4[0], CDR_q_4[1], CDR_q_4[2], CDR_q_3[0], CDR_q_3[1], CDR_q_3[2], CDR_q_2, CDR_q}),
    .clk(not_6_out));  // open: clr
  // NOT_Gate not_7 is placed but not wired

  // Notes on the sheet:
  //   AR
  //   AND
  //   OR
  //   Xor
  //   Not
  //   Adder
  //   Substracter
  //   SHR
  //   SHL
  //   PC
  //   MEMORY
  //   DR
  //   PADDING
  //   Output of ALU
  //   AC
  //   br1
  //   br0
  //   cd1
  //   cd0
  //   load AC
  //   load AR
  //   MAPPING
  //   load DR
  //   F!
  //   F2
  //   F3
  //   contents of rom_1 (hex, n*v repeats v):
  //   c3 10602 20640 640 206 640 c3 3640 643 1460a e0640 640 c3 2060e 9460f e0640 48*0 c0641 12e42 a0780
  //   10644 a0700
endmodule
